// Logisim project new.circ as structural Verilog: 4 circuits, main circuit main
module main (
  input  in_1,
  input  in_2
);

  wire clock_1_out;
  wire [2:0] decoder_1_funct3;
  wire [4:0] decoder_1_rd, decoder_1_rs1, decoder_1_rs2;
  wire [6:0] decoder_1_imm, decoder_1_opcode;
  wire [11:0] imm_gen_1_itype, imm_gen_1_sbtype, imm_gen_1_stype;
  wire [19:0] imm_gen_1_ujtype, imm_gen_1_utype;
  wire [31:0] adder_1_out, ram_1_data, register_1_q;

  Clock #(.highDuration(4), .lowDuration(4)) clock_1 (.out(clock_1_out));
  Register #(.width(32)) register_1 (.D(adder_1_out), .en(in_1), .Q(register_1_q), .clk(clock_1_out), .clr(in_2));
  Adder #(.width(32)) adder_1 (.a(register_1_q), .b(32'h4), .out(adder_1_out));  // open: cin, cout
  RAM #(.addrWidth(24), .dataWidth(32)) ram_1 (
    .addr(register_1_q[25:2]), .data(ram_1_data), .sel(in_1), .clk(clock_1_out), .ld(in_2), .clr(in_2));
  decoder decoder_1 (
    .ins(ram_1_data), .opcode(decoder_1_opcode), .rd(decoder_1_rd), .funct3(decoder_1_funct3),
    .rs1(decoder_1_rs1), .rs2(decoder_1_rs2), .imm(decoder_1_imm));
  imm_gen imm_gen_1 (
    .ins(ram_1_data), .Itype(imm_gen_1_itype), .Stype(imm_gen_1_stype), .SBtype(imm_gen_1_sbtype),
    .Utype(imm_gen_1_utype), .UJtype(imm_gen_1_ujtype));
endmodule

module Control_Unit (
  input  [6:0] in_1,
  output ALUSrc,
  output MemtoReg,
  output RegWrite,
  output MemRead,
  output MemWrite,
  output Branch,
  output ALU1,
  output ALU0
);

  wire and_1_out, and_2_out, and_3_out, and_4_out, and_5_out, and_6_out, and_7_out, and_8_out, and_9_out,
       and_10_out, and_11_out, and_12_out, and_13_out, and_14_out, and_15_out, and_16_out, and_17_out,
       and_18_out, and_19_out, and_20_out, and_21_out, and_22_out, and_23_out, and_24_out, and_25_out,
       and_26_out, and_27_out, and_28_out, and_29_out, and_30_out, and_31_out, and_32_out, and_33_out,
       and_34_out, and_35_out, and_36_out, and_37_out, and_38_out, and_39_out, and_40_out, and_41_out,
       and_42_out, and_43_out, and_44_out, and_47_out, and_48_out, not_1_out, not_2_out, not_3_out,
       not_4_out, not_5_out, not_6_out, not_7_out, not_8_out, not_9_out, not_10_out, not_11_out, not_12_out,
       not_13_out, not_14_out, not_15_out, not_16_out, not_17_out, not_18_out, not_19_out, not_20_out,
       not_21_out, not_22_out, not_23_out, not_24_out, not_25_out, not_26_out, not_27_out, not_28_out,
       not_29_out, not_30_out, not_31_out, not_32_out, not_33_out, not_34_out, not_35_out;

  RAM #(.bus("separate")) ram_1 ();  // open: addr, din, data, str, sel, clk, ld, clr
  not not_1 (not_1_out, in_1[3]);
  not not_2 (not_2_out, in_1[4]);
  not not_3 (not_3_out, in_1[2]);
  not not_4 (not_4_out, in_1[3]);
  not not_5 (not_5_out, in_1[4]);
  not not_6 (not_6_out, in_1[5]);
  not not_7 (not_7_out, in_1[2]);
  not not_8 (not_8_out, in_1[3]);
  not not_9 (not_9_out, in_1[4]);
  not not_10 (not_10_out, in_1[5]);
  not not_11 (not_11_out, in_1[2]);
  not not_12 (not_12_out, in_1[3]);
  not not_13 (not_13_out, in_1[2]);
  not not_14 (not_14_out, in_1[3]);
  not not_15 (not_15_out, in_1[4]);
  not not_16 (not_16_out, in_1[5]);
  not not_17 (not_17_out, in_1[2]);
  not not_18 (not_18_out, in_1[3]);
  not not_19 (not_19_out, in_1[4]);
  not not_20 (not_20_out, in_1[2]);
  not not_21 (not_21_out, in_1[3]);
  not not_22 (not_22_out, in_1[4]);
  not not_23 (not_23_out, in_1[2]);
  not not_24 (not_24_out, in_1[3]);
  not not_25 (not_25_out, in_1[2]);
  not not_26 (not_26_out, in_1[3]);
  not not_27 (not_27_out, in_1[4]);
  and and_1 (and_1_out, in_1[0], in_1[1]);
  not not_28 (not_28_out, in_1[2]);
  and and_2 (and_2_out, not_1_out, not_2_out);
  not not_29 (not_29_out, in_1[6]);
  and and_3 (and_3_out, in_1[0], in_1[1]);
  and and_4 (and_4_out, not_3_out, not_4_out);
  and and_5 (and_5_out, not_5_out, not_6_out);
  not not_30 (not_30_out, in_1[6]);
  and and_6 (and_6_out, in_1[0], in_1[1]);
  and and_7 (and_7_out, not_7_out, not_8_out);
  and and_8 (and_8_out, not_9_out, not_10_out);
  not not_31 (not_31_out, in_1[6]);
  and and_9 (and_9_out, in_1[0], in_1[1]);
  and and_10 (and_10_out, not_11_out, not_12_out);
  and and_11 (and_11_out, in_1[4], in_1[5]);
  not not_32 (not_32_out, in_1[6]);
  and and_12 (and_12_out, in_1[0], in_1[1]);
  and and_13 (and_13_out, not_13_out, not_14_out);
  and and_14 (and_14_out, not_15_out, not_16_out);
  not not_33 (not_33_out, in_1[6]);
  and and_15 (and_15_out, in_1[0], in_1[1]);
  and and_16 (and_16_out, not_17_out, not_18_out);
  and and_17 (and_17_out, not_19_out, in_1[5]);
  not not_34 (not_34_out, in_1[6]);
  and and_18 (and_18_out, in_1[0], in_1[1]);
  and and_19 (and_19_out, not_20_out, not_21_out);
  and and_20 (and_20_out, not_22_out, in_1[5]);
  and and_21 (and_21_out, in_1[0], in_1[1]);
  and and_22 (and_22_out, not_23_out, not_24_out);
  and and_23 (and_23_out, in_1[4], in_1[5]);
  not not_35 (not_35_out, in_1[6]);
  and and_24 (and_24_out, in_1[0], in_1[1]);
  and and_25 (and_25_out, not_25_out, not_26_out);
  and and_26 (and_26_out, not_27_out, in_1[5]);
  and and_27 (and_27_out, and_1_out, not_28_out);
  and and_28 (and_28_out, and_2_out, not_29_out);
  and and_29 (and_29_out, and_3_out, and_4_out);
  and and_30 (and_30_out, and_5_out, not_30_out);
  and and_31 (and_31_out, and_6_out, and_7_out);
  and and_32 (and_32_out, and_8_out, not_31_out);
  and and_33 (and_33_out, and_9_out, and_10_out);
  and and_34 (and_34_out, and_11_out, not_32_out);
  and and_35 (and_35_out, and_12_out, and_13_out);
  and and_36 (and_36_out, and_14_out, not_33_out);
  and and_37 (and_37_out, and_15_out, and_16_out);
  and and_38 (and_38_out, and_17_out, not_34_out);
  and and_39 (and_39_out, and_18_out, and_19_out);
  and and_40 (and_40_out, and_20_out, in_1[6]);
  and and_41 (and_41_out, and_21_out, and_22_out);
  and and_42 (and_42_out, and_23_out, not_35_out);
  and and_43 (and_43_out, and_24_out, and_25_out);
  and and_44 (and_44_out, and_26_out, in_1[6]);
  and and_45 (ALUSrc, and_27_out, and_28_out);
  and and_46 (MemtoReg, and_29_out, and_30_out);
  and and_47 (and_47_out, and_31_out, and_32_out);
  and and_48 (and_48_out, and_33_out, and_34_out);
  and and_49 (MemRead, and_35_out, and_36_out);
  and and_50 (MemWrite, and_37_out, and_38_out);
  and and_51 (Branch, and_39_out, and_40_out);
  and and_52 (ALU1, and_41_out, and_42_out);
  and and_53 (ALU0, and_43_out, and_44_out);
  or or_1 (RegWrite, and_47_out, and_48_out);
endmodule

// DECODER
module decoder (
  input  [31:0] ins,
  output [6:0] opcode,
  output [4:0] rd,
  output [2:0] funct3,
  output [4:0] rs1,
  output [4:0] rs2,
  output [6:0] imm
);


  assign funct3 = ins[14:12];
  assign imm = ins[31:25];
  assign opcode = ins[6:0];
  assign rd = ins[11:7];
  assign rs1 = ins[19:15];
  assign rs2 = ins[24:20];
endmodule

// IMM GEN
module imm_gen (
  input  [31:0] ins,
  output [11:0] Itype,
  output [11:0] Stype,
  output [11:0] SBtype,
  output [19:0] Utype,
  output [19:0] UJtype
);

  wire comparator_1_eq, comparator_8_eq, comparator_9_eq, comparator_10_eq, comparator_12_eq;

  Comparator #(.width(7)) comparator_1 (.a(7'b0000011), .b(ins[6:0]), .eq(comparator_1_eq));  // open: gt, lt
  Comparator #(.width(7)) comparator_2 (.a(7'b0001111), .b(ins[6:0]), .eq(comparator_1_eq));  // open: gt, lt
  Comparator #(.width(7)) comparator_3 (.a(7'b0001101), .b(ins[6:0]), .eq(comparator_1_eq));  // open: gt, lt
  Comparator #(.width(7)) comparator_4 (.a(7'b0011011), .b(ins[6:0]), .eq(comparator_1_eq));  // open: gt, lt
  Comparator #(.width(7)) comparator_5 (.a(7'b0010111), .b(ins[6:0]), .eq(comparator_1_eq));  // open: gt, lt
  Comparator #(.width(7)) comparator_6 (.a(7'b1000011), .b(ins[6:0]), .eq(comparator_1_eq));  // open: gt, lt
  Comparator #(.width(7)) comparator_7 (.a(7'b1001001), .b(ins[6:0]), .eq(comparator_1_eq));  // open: gt, lt
  Comparator #(.width(7)) comparator_8 (.a(7'b0010111), .b(ins[6:0]), .eq(comparator_8_eq));  // open: gt, lt
  Comparator #(.width(7)) comparator_9 (
    .a(7'b0111111), .b(ins[6:0]), .eq(comparator_9_eq), .lt(comparator_9_eq));  // open: gt
  Comparator #(.width(7)) comparator_10 (.a(7'b0010001), .b(ins[6:0]), .eq(comparator_10_eq));  // open: gt, lt
  Comparator #(.width(7)) comparator_11 (.a(7'b0100101), .b(ins[6:0]), .eq(comparator_10_eq));  // open: gt, lt
  Comparator #(.width(7)) comparator_12 (.a(7'b1101111), .b(ins[6:0]), .eq(comparator_12_eq));  // open: gt, lt
  Multiplexer #(.width(12)) multiplexer_1 (.in1(ins[31:20]), .out(Itype), .en(comparator_1_eq));  // open: in0, sel
  Multiplexer #(.width(12)) multiplexer_2 (
    .in1({ins[31:25], ins[11:7]}), .out(Stype), .en(comparator_8_eq));  // open: in0, sel
  Multiplexer #(.width(12)) multiplexer_3 (
    .in1({ins[31:25], ins[11:7]}), .out(SBtype), .en(comparator_9_eq));  // open: in0, sel
  Multiplexer #(.width(20)) multiplexer_4 (.in1(ins[31:12]), .out(Utype), .en(comparator_10_eq));  // open: in0, sel
  Multiplexer #(.width(20)) multiplexer_5 (.in1(ins[31:12]), .out(UJtype), .en(comparator_12_eq));  // open: in0, sel
endmodule
